// Logisim project q2.circ as structural Verilog: 1 circuit, main circuit main
module main (
  input  in_1,
  input  Using_NAND,
  input  in_3,
  input  in_4,
  input  in_5,
  input  in_6,
  input  in_7,
  input  in_8,
  input  in_9,
  input  in_10,
  input  in_11,
  input  in_12,
  input  Using_NOR,
  input  in_14,
  input  in_15,
  input  in_16,
  input  in_17,
  input  in_18,
  input  in_19,
  input  in_20,
  input  in_21,
  input  in_22,
  input  in_23,
  input  in_24,
  input  in_25,
  input  in_26
);

  wire nand_1_out, nand_2_out, nand_3_out, nand_4_out, nand_5_out, nand_6_out, nand_7_out, nand_8_out,
       nand_9_out, nand_10_out, nand_11_out, nand_12_out, nand_13_out, nand_14_out, nand_15_out, nand_16_out,
       nand_17_out, nand_18_out, nand_19_out, nand_20_out, nor_1_out, nor_2_out, nor_3_out, nor_4_out,
       nor_5_out, nor_6_out, nor_7_out, nor_8_out, nor_9_out, nor_10_out, nor_11_out, nor_12_out, nor_13_out,
       nor_14_out, nor_15_out, nor_16_out, nor_17_out, nor_18_out, nor_19_out, nor_20_out;

  nor nor_1 (nor_1_out, in_5, in_5);
  nor nor_2 (nor_2_out, in_7, in_7);
  nand nand_1 (nand_1_out, Using_NAND, in_3, in_3);
  nand nand_2 (nand_2_out, in_9, in_9);
  nand nand_3 (nand_3_out, in_11, in_11);
  nor nor_3 (nor_3_out, Using_NOR, in_14);
  nand nand_4 (nand_4_out, in_17, in_17);
  nor nor_4 (nor_4_out, in_20, in_20);
  nor nor_5 (nor_5_out, nor_1_out, nor_2_out);
  nand nand_5 (nand_5_out, nand_2_out, nand_3_out);
  nand nand_6 (nand_6_out, nand_1_out, nand_1_out, nand_1_out, nand_1_out);
  LED led_1 (.in(nor_5_out));
  LED led_2 (.in(nand_5_out));
  nor nor_6 (nor_6_out, nor_3_out, nor_3_out);
  LED led_3 (.in(nand_4_out));
  LED led_4 (.in(nor_4_out));
  LED led_5 (.in(nand_6_out));
  LED led_6 (.in(nor_6_out));
  nand nand_7 (nand_7_out, in_23, in_24);
  nor nor_7 (nor_7_out, in_25, in_26);
  nand nand_8 (nand_8_out, in_23, nand_7_out);
  nand nand_9 (nand_9_out, nand_7_out, in_24);
  nor nor_8 (nor_8_out, in_25, nor_7_out);
  nor nor_9 (nor_9_out, nor_7_out, in_26);
  nand nand_10 (nand_10_out, nand_8_out, nand_9_out);
  nor nor_10 (nor_10_out, in_6, in_6);
  nor nor_11 (nor_11_out, in_8, in_8);
  nand nand_11 (nand_11_out, in_10, in_10);
  nand nand_12 (nand_12_out, in_12, in_12);
  nor nor_12 (nor_12_out, in_15, in_16);
  nand nand_13 (nand_13_out, in_18, in_19);
  nor nor_13 (nor_13_out, in_21, in_22);
  nor nor_14 (nor_14_out, nor_8_out, nor_9_out);
  nand nand_14 (nand_14_out, in_1, in_4);
  nor nor_15 (nor_15_out, nor_10_out, nor_11_out);
  nor nor_16 (nor_16_out, in_21, nor_13_out);
  nor nor_17 (nor_17_out, nor_13_out, in_22);
  nand nand_15 (nand_15_out, nand_10_out, nand_10_out);
  LED led_7 (.in(nor_14_out));
  LED led_8 (.in(nand_14_out));
  nand nand_16 (nand_16_out, nand_11_out, nand_12_out);
  LED led_9 (.in(nor_12_out));
  nand nand_17 (nand_17_out, in_18, nand_13_out);
  nand nand_18 (nand_18_out, nand_13_out, in_19);
  nor nor_18 (nor_18_out, nor_15_out, nor_15_out);
  LED led_10 (.in(nand_15_out));
  LED led_11 (.in(nor_18_out));
  nand nand_19 (nand_19_out, nand_16_out, nand_16_out);
  LED led_12 (.in(nand_19_out));
  nand nand_20 (nand_20_out, nand_17_out, nand_18_out);
  nor nor_19 (nor_19_out, nor_16_out, nor_17_out);
  LED led_13 (.in(nand_20_out));
  nor nor_20 (nor_20_out, nor_19_out, nor_19_out);
  LED led_14 (.in(nor_20_out));

  // Notes on the sheet:
  //   AND GATE:
  //   OR GATE:
  //   NOT GATE:
  //   Using NOR
  //   Using NAND
  //   Using NAND
  //   Using NOR
  //   XNOR GATE:
  //   Using NAND
  //   Using NOR
  //   NAND GATE:
  //   NOR GATE:
  //   XOR GATE:
  //   Using NAND
  //   Using NOR
  //   Using NAND
  //   Using NOR
  //   Using NAND
  //   Using NOR
endmodule
