// Logisim project fp_adder.circ as structural Verilog: 1 circuit, main circuit main
module main (
  input  [22:0] in_1,
  input  [22:0] in_2,
  input  in_3,
  input  [7:0] in_4,
  input  in_5,
  input  [7:0] in_6,
  output out_7,
  output [4:0] out_8,
  output [22:0] out_9,
  output out_10,
  output [7:0] out_11
);

  wire comparator_1_gt, comparator_2_gt, multiplexer_3_out, multiplexer_4_out, xnor_1_out;
  wire [0:0] multiplexer_14_out;
  wire [4:0] adder_2_out, bitfinder_1_index;
  wire [7:0] adder_5_out, multiplexer_1_out, multiplexer_2_out, multiplexer_6_out, subtractor_1_out,
       subtractor_2_out, subtractor_3_out;
  wire [22:0] multiplexer_7_out, multiplexer_10_out;
  wire [23:0] adder_4_out, multiplexer_11_out, multiplexer_14_out_2, shifter_2_out;
  wire [24:0] adder_1_out, adder_3_out, adder_6_out, multiplexer_8_out, multiplexer_13_out, not_1_out,
       not_2_out, not_3_out, shifter_1_out, shifter_3_out;
  wire [24:24] adder_4_out_2, multiplexer_11_out_2;

  xnor xnor_1 (xnor_1_out, in_3, in_5);
  Subtractor subtractor_1 (.a(in_4), .b(in_6), .out(subtractor_1_out));  // open: bin, bout
  Comparator #(.mode("unsigned")) comparator_1 (.a(in_4), .b(in_6), .gt(comparator_1_gt));  // open: eq, lt
  Subtractor subtractor_2 (.a(in_6), .b(in_4), .out(subtractor_2_out));  // open: bin, bout
  Multiplexer #(.width(8), .enable("false")) multiplexer_1 (
    .in0(subtractor_2_out), .in1(subtractor_1_out), .out(multiplexer_1_out), .sel(comparator_1_gt));
  Multiplexer #(.width(8), .enable("false")) multiplexer_2 (
    .in0(in_6), .in1(in_4), .out(multiplexer_2_out), .sel(comparator_1_gt));
  Multiplexer #(.enable("false")) multiplexer_3 (
    .in0(in_5), .in1(in_3), .out(multiplexer_3_out), .sel(comparator_1_gt));
  Multiplexer #(.enable("false")) multiplexer_4 (
    .in0(in_3), .in1(in_5), .out(multiplexer_4_out), .sel(comparator_1_gt));
  Multiplexer #(.enable("false")) multiplexer_5 (.in0(adder_4_out_2[24]), .in1(in_3), .out(out_10), .sel(xnor_1_out));
  Comparator comparator_2 (.a(multiplexer_1_out), .b(8'h17), .gt(comparator_2_gt));  // open: eq, lt
  Multiplexer #(.width(8), .enable("false")) multiplexer_6 (
    .in0(multiplexer_1_out), .in1(8'h17), .out(multiplexer_6_out), .sel(comparator_2_gt));
  Multiplexer #(.width(23), .enable("false")) multiplexer_7 (
    .in0(in_2), .in1(in_1), .out(multiplexer_7_out), .sel(comparator_1_gt));
  assign not_1_out = ~{2'b01, multiplexer_7_out};  // NOT_Gate not_1, 25 bits wide
  Multiplexer #(.width(25), .enable("false")) multiplexer_8 (
    .in0({2'b01, multiplexer_7_out}), .in1(adder_1_out), .out(multiplexer_8_out), .sel(multiplexer_3_out));
  BitFinder #(.width(24), .\type ("high1")) bitfinder_1 (
    .in(multiplexer_11_out), .index(bitfinder_1_index));  // open: found
  Subtractor subtractor_3 (.a(multiplexer_2_out), .b({3'b000, out_8}), .out(subtractor_3_out));  // open: bin, bout
  Multiplexer #(.width(8), .enable("false")) multiplexer_9 (
    .in0(subtractor_3_out), .in1(adder_5_out), .out(out_11), .sel(xnor_1_out));
  Multiplexer #(.width(23), .disabled(0), .enable("false")) multiplexer_10 (
    .in0(in_1), .in1(in_2), .out(multiplexer_10_out), .sel(comparator_1_gt));
  Adder #(.width(25)) adder_1 (.a(not_1_out), .b(25'h1), .out(adder_1_out));  // open: cin, cout
  Subtractor #(.width(5)) subtractor_4 (.a(5'b10111), .b(bitfinder_1_index), .out(out_8));  // open: bin, bout
  Shifter #(.width(25), .shift("lr")) shifter_1 (
    .in({2'b01, multiplexer_10_out}), .\dist (multiplexer_6_out[4:0]), .out(shifter_1_out));
  assign not_2_out = ~shifter_1_out;  // NOT_Gate not_2, 25 bits wide
  Multiplexer #(.width(25), .enable("false")) multiplexer_11 (
    .in0({adder_4_out_2[24], adder_4_out}), .in1(adder_6_out),
    .out({multiplexer_11_out_2[24], multiplexer_11_out}), .sel(adder_4_out_2[24]));
  Adder #(.width(5)) adder_2 (.a(out_8), .b(5'b00001), .out(adder_2_out));  // open: cin, cout
  Multiplexer #(.width(23), .enable("false")) multiplexer_12 (
    .in0(shifter_2_out[23:1]), .in1(shifter_3_out[22:0]), .out(out_9), .sel(xnor_1_out));
  Adder #(.width(25)) adder_3 (.a(not_2_out), .b(25'h1), .out(adder_3_out));  // open: cin, cout
  Multiplexer #(.width(25), .enable("false")) multiplexer_13 (
    .in0(shifter_1_out), .in1(adder_3_out), .out(multiplexer_13_out), .sel(multiplexer_4_out));
  Adder #(.width(25)) adder_4 (
    .a(multiplexer_13_out), .b(multiplexer_8_out), .out({adder_4_out_2[24], adder_4_out}), .cout(out_7));  // open: cin
  Shifter #(.width(24)) shifter_2 (.in(multiplexer_11_out), .\dist (adder_2_out), .out(shifter_2_out));
  assign not_3_out = ~{adder_4_out_2[24], adder_4_out};  // NOT_Gate not_3, 25 bits wide
  Adder adder_5 (.a(multiplexer_2_out), .b({{7{1'b0}}, multiplexer_14_out[0]}), .out(adder_5_out));  // open: cin, cout
  Adder #(.width(25)) adder_6 (.a(not_3_out), .b(25'h1), .out(adder_6_out));  // open: cin, cout
  Multiplexer #(.width(25), .enable("false")) multiplexer_14 (
    .in0({adder_4_out_2[24], adder_4_out}), .in1(adder_6_out),
    .out({multiplexer_14_out[0], multiplexer_14_out_2}), .sel(out_7));
  Shifter #(.width(25), .shift("lr")) shifter_3 (
    .in({multiplexer_14_out[0], multiplexer_14_out_2}), .\dist ({4'b0000, multiplexer_14_out[0]}),
    .out(shifter_3_out));
endmodule
